# Fritzing sketch pcdDesign (saved by Fritzing 0.9.3b)
circuit board: 2.7cm x 8.4cm
breadboards: 1

parts:
  GY1 = MPU-6050 Board GY-521 [form="♀ (female)" package=THT]
  R4 = Resistor [tolerance=±5% resistance=1k package=THT]
  LED1 = RGB LED (com. cathode, rgb) [package="5 mm [THT]"]
  R3 = Resistor [tolerance=±5% resistance=1k package=THT]
  R5 = Resistor [tolerance=±5% resistance=1k package=THT]
  U1 = NodeMCU V1.0
  Part1 = TP4056 Charger
  S1 = Toggle Switch [package=THT]
  VCC1 = Battery

nets:
  N1: GY1.pin1, U1.Vin, S1.L1
  N2: GY1.pin2, LED1.common_cathode, U1.GND, Part1.IN-, Part1.BAT-, VCC1.-
  N3: GY1.pin3, U1.D2
  N4: GY1.pin4, U1.D1
  N5: R4.Pin_0, LED1.green_anode
  N6: R4.Pin_1, U1.D6
  N7: LED1.red_anode, R3.Pin_0
  N8: LED1.blue_anode, R5.Pin_0
  N9: R3.Pin_1, U1.D5
  N10: R5.Pin_1, U1.D7
  N11: Part1.BAT+, S1.COM, VCC1.+

custom parts:
  MPU-6050 Board GY-521: Acelerometro y Giroscopio MPU-6050 Board GY-521
  NodeMCU V1.0: ESP8266 based NodeMCU
